// Logisim project PROJECT 2 DDCA LOGISM DIAGRAM.circ as structural Verilog: 1 circuit, main circuit main
module main (
  input  D,
  input  M,
  input  A,
  input  S
);

  wire AND_out, or_2_out, OR_out;

  or OR (OR_out, D, M);
  and AND (AND_out, OR_out, A);
  or or_2 (or_2_out, AND_out, S);
  LED ALARM (.in(or_2_out));

  // Notes on the sheet:
  //   OR 1: D OR M
  //   ALARM = S PR [ A AND (D OR M) ]
  //   AND: A AND (D OR M)
  //   OR 2: AND OR S
  //   OUTPUT LED
endmodule
