// Logisim project full subtractor.circ as structural Verilog: 1 circuit, main circuit main
module main (
  input  a,
  input  b,
  input  bin,
  output d,
  output bout
);

  wire and_1_out, and_2_out, not_1_out, not_2_out, xor_1_out;

  not not_1 (not_1_out, b);
  xor xor_1 (xor_1_out, b, bin);
  and and_1 (and_1_out, not_1_out, bin);
  xor xor_2 (d, a, xor_1_out);
  not not_2 (not_2_out, xor_1_out);
  and and_2 (and_2_out, not_2_out, a);
  or or_1 (bout, and_2_out, and_1_out);
endmodule
