// Logisim project half adder.circ as structural Verilog: 1 circuit, main circuit main
module main (
  input  a,
  input  b,
  output sum,
  output c
);

  xor xor_1 (sum, a, b);
  and and_1 (c, a, b);

  // Notes on the sheet:
  //   half adder
  //   xor
endmodule
