// Logisim project half subtractor.circ as structural Verilog: 1 circuit, main circuit main
module main (
  input  a,
  input  b,
  output difference,
  output borrow
);

  wire not_1_out;

  not not_1 (not_1_out, a);
  xor xor_1 (difference, a, b);
  and and_1 (borrow, not_1_out, b);

  // Notes on the sheet:
  //   xor
  //   and
endmodule
